# Fritzing sketch Untitled Sketch1 (saved by Fritzing 0.9.3b)

parts:
  LED1 = LED_RING [package=led_ring]
  A1 = Pzem-004t-pins
  Part1 = Adafruit ESP32-S3 Feather [part_number="Adafruit #5323"]
  BULB1 = LEDs [package=led10mm]  # not connected
  KY-1 = Keyes Relay [package=THT]
  U1 = Voltage Regulator - 5V [package="DPak [SMD]"]
  VCC1 = Battery block 9V

nets:
  N1: LED1.4, A1.CT-2
  N2: LED1.6, A1.CT-1
  N3: A1.RX, Part1.TX
  N4: A1.TX, Part1.RX
  N5: A1.CF, Part1.A4
  GND: A1.GND#8, Part1.GND, U1.GND, VCC1.-
  N6: Part1.A5, KY-1.signal
  N7: Part1.3.3V, U1.output_voltage
  N8: U1.input_voltage, VCC1.+

notes:
  230 V

custom parts:
  Pzem-004t-pins: PZEM-004T 100A AC 80-260V Digital Voltmeter Ammeter Wattmeter Digital Multifunctional Test Pulse Communication TTL Serial Module.
  Adafruit ESP32-S3 Feather: The ESP32-S3 has arrived in Feather format - and what a great way to get started with this powerful new chip from Espressif! With dual 240 MHz cores, WiFi and BLE support, and native USB, this Feather is great for powering your IoT projects. That's right - it's the new Adafruit ESP32-S3 Feather! With native USB and 8 MB flash, this board will let you upgrade your existing ESP32 projects.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
  Keyes Relay: The Keyes 5V relay module is suitable for SCM development, home appliance control. It uses a 5V~12V TIL control signal which can control DC / AC signal.
